// Logisim project ex5.circ as structural Verilog: 5 circuits, main circuit rotr
module rotr (
  input  [15:0] A,
  input  [3:0] B,
  output [15:0] Out1
);

  wire [15:0] rot1_1_out_2, rot1_2_out_2, rot1_3_out_2, rot1_4_out_2, rot1_5_out_2, rot1_6_out_2,
       rot1_7_out_2, rot1_8_out_2, rot2_1_out_2, rot2_2_out_2, rot2_3_out_2, rot2_4_out_2, rot2_5_out_2,
       rot2_6_out_2, rot2_7_out_2, rot2_8_out_2, rot4_1_out_2, rot4_2_out_2, rot4_3_out_2, rot4_4_out_2,
       rot4_5_out_2, rot4_6_out_2, rot4_7_out_2, rot4_8_out_2, rot8_1_out_2, rot8_2_out_2, rot8_3_out_2,
       rot8_4_out_2, rot8_5_out_2, rot8_6_out_2, rot8_7_out_2, rot8_8_out_2;

  rot1 rot1_1 (.in_1(A), .out_2(rot1_1_out_2));
  rot1 rot1_2 (.in_1(A), .out_2(rot1_2_out_2));
  rot4 rot4_1 (.in_1(A), .out_2(rot4_1_out_2));
  rot1 rot1_3 (.in_1(A), .out_2(rot1_3_out_2));
  rot2 rot2_1 (.in_1(A), .out_2(rot2_1_out_2));
  rot1 rot1_4 (.in_1(A), .out_2(rot1_4_out_2));
  rot8 rot8_1 (.in_1(A), .out_2(rot8_1_out_2));
  rot1 rot1_5 (.in_1(A), .out_2(rot1_5_out_2));
  rot2 rot2_2 (.in_1(A), .out_2(rot2_2_out_2));
  rot1 rot1_6 (.in_1(A), .out_2(rot1_6_out_2));
  rot4 rot4_2 (.in_1(A), .out_2(rot4_2_out_2));
  rot1 rot1_7 (.in_1(A), .out_2(rot1_7_out_2));
  rot2 rot2_3 (.in_1(A), .out_2(rot2_3_out_2));
  rot1 rot1_8 (.in_1(A), .out_2(rot1_8_out_2));
  rot2 rot2_4 (.in_1(A), .out_2(rot2_4_out_2));
  rot2 rot2_5 (.in_1(rot1_2_out_2), .out_2(rot2_5_out_2));
  rot4 rot4_3 (.in_1(rot1_3_out_2), .out_2(rot4_3_out_2));
  rot4 rot4_4 (.in_1(rot2_1_out_2), .out_2(rot4_4_out_2));
  rot2 rot2_6 (.in_1(rot1_4_out_2), .out_2(rot2_6_out_2));
  rot8 rot8_2 (.in_1(rot1_5_out_2), .out_2(rot8_2_out_2));
  rot8 rot8_3 (.in_1(rot2_2_out_2), .out_2(rot8_3_out_2));
  rot2 rot2_7 (.in_1(rot1_6_out_2), .out_2(rot2_7_out_2));
  rot8 rot8_4 (.in_1(rot4_2_out_2), .out_2(rot8_4_out_2));
  rot4 rot4_5 (.in_1(rot1_7_out_2), .out_2(rot4_5_out_2));
  rot4 rot4_6 (.in_1(rot2_3_out_2), .out_2(rot4_6_out_2));
  rot2 rot2_8 (.in_1(rot1_8_out_2), .out_2(rot2_8_out_2));
  rot4 rot4_7 (.in_1(rot2_6_out_2), .out_2(rot4_7_out_2));
  rot8 rot8_5 (.in_1(rot2_7_out_2), .out_2(rot8_5_out_2));
  rot8 rot8_6 (.in_1(rot4_5_out_2), .out_2(rot8_6_out_2));
  rot8 rot8_7 (.in_1(rot4_6_out_2), .out_2(rot8_7_out_2));
  rot4 rot4_8 (.in_1(rot2_8_out_2), .out_2(rot4_8_out_2));
  rot8 rot8_8 (.in_1(rot4_8_out_2), .out_2(rot8_8_out_2));
  Multiplexer #(.select(4), .width(16), .enable("false")) multiplexer_1 (
    .in0(A), .in1(rot1_1_out_2), .in2(rot2_4_out_2), .in3(rot2_5_out_2), .in4(rot4_1_out_2),
    .in5(rot4_3_out_2), .in6(rot4_4_out_2), .in7(rot4_7_out_2), .in8(rot8_1_out_2), .in9(rot8_2_out_2),
    .in10(rot8_3_out_2), .in11(rot8_5_out_2), .in12(rot8_4_out_2), .in13(rot8_6_out_2), .in14(rot8_7_out_2),
    .in15(rot8_8_out_2), .out(Out1), .sel(B));

  // Notes on the sheet:
  //   PUT CIRCUITRY HERE
endmodule

module rot8 (
  input  [15:0] in_1,
  output [15:0] out_2
);


  assign out_2 = {in_1[7:0], in_1[15:8]};

  // Notes on the sheet:
  //   PUT CIRCUITRY HERE
endmodule

module rot4 (
  input  [15:0] in_1,
  output [15:0] out_2
);


  assign out_2 = {in_1[3:0], in_1[15:4]};

  // Notes on the sheet:
  //   PUT CIRCUITRY HERE
endmodule

module rot2 (
  input  [15:0] in_1,
  output [15:0] out_2
);


  assign out_2 = {in_1[1:0], in_1[15:2]};

  // Notes on the sheet:
  //   PUT CIRCUITRY HERE
endmodule

module rot1 (
  input  [15:0] in_1,
  output [15:0] out_2
);


  assign out_2 = {in_1[0], in_1[15:1]};

  // Notes on the sheet:
  //   PUT CIRCUITRY HERE
endmodule
